# Fritzing sketch pcb (saved by Fritzing 1.0.6)
circuit board: 5.29914cm x 2.07346cm
breadboards: 1

parts:
  U1 = attiny85 [package=dip]
  Q1 = TRANSISTOR_NPN [package=to-92]
  Q2 = TRANSISTOR_NPN [package=to-92]
  LED1 = LED - 5mm [color="Red (633nm)" current=0.030A package="5 mm [THT]"]
  R2 = Resistor [tolerance=±5% power=0.25W resistance=220 package=THT]
  R1 = Resistor [tolerance=±5% power=0.25W resistance=220 package=THT]
  USB-C = Adafruit USB Type C Plug Breakout [mn=Adafruit mpn=#5978 part_number=#5978]
  LED2 = LED - 5mm [color="Red (633nm)" current=0.030A package="5 mm [THT]"]
  S1 = Momentary Switch [package=ksa_sealed_tac_switch]

nets:
  N1: U1.Pin_1, S1.3, S1.4
  N2: U1.Pin_4, Q1.E, Q2.E, USB-C.GND, S1.1, S1.2
  N3: U1.Pin_5, R2.Pin_0
  N4: U1.Pin_6, R1.Pin_0
  N5: U1.Pin_8, LED1.anode, USB-C.VBUS, LED2.anode
  N6: Q1.B, R1.Pin_1
  N7: Q1.C, LED1.cathode
  N8: Q2.B, R2.Pin_1
  N9: Q2.C, LED2.cathode
